# Fritzing sketch clockobin (saved by Fritzing 0.9.2b)
breadboards: 1

parts:
  VCC1 = Battery
  LED1 = LED - 5mm [color="Blue (525nm)" package="5 mm [THT]"]
  LED2 = LED - 5mm [color="Green (570nm)" package="5 mm [THT]"]
  LED3 = LED - 5mm [color="Yellow (595nm)" package="5 mm [THT]"]
  LED4 = LED - 5mm [color="Orange (605nm)" package="5 mm [THT]"]
  LED5 = LED - 5mm [color="Red (633nm)" package="5 mm [THT]"]
  LED6 = LED - 5mm [color="Yellow (595nm)" package="5 mm [THT]"]
  LED7 = LED - 5mm [color="Orange (605nm)" package="5 mm [THT]"]
  LED8 = LED - 5mm [color="Green (570nm)" package="5 mm [THT]"]
  LED9 = LED - 5mm [color="Blue (525nm)" package="5 mm [THT]"]
  LED10 = LED - 5mm [color="Red (633nm)" package="5 mm [THT]"]
  LED11 = LED - 5mm [color="White (6500K)" package="5 mm [THT]"]
  R1 = Resistor [tolerance=±5% resistance=220 package=THT]
  R2 = Resistor [tolerance=±5% resistance=220 package=THT]
  R3 = Resistor [tolerance=±5% resistance=220 package=THT]
  R4 = Resistor [tolerance=±5% resistance=220 package=THT]
  R5 = Resistor [tolerance=±5% resistance=220 package=THT]
  R6 = Resistor [tolerance=±5% resistance=220 package=THT]
  R7 = Resistor [tolerance=±5% resistance=220 package=THT]
  R8 = Resistor [tolerance=±5% resistance=220 package=THT]
  R9 = Resistor [tolerance=±5% resistance=220 package=THT]
  R10 = Resistor [tolerance=±5% resistance=220 package=THT]
  R11 = Resistor [tolerance=±5% resistance=220 package=THT]
  Composant1 = Arduino Nano (Rev3.0)

nets:
  N1: VCC1.-, LED1.cathode, LED2.cathode, LED3.cathode, LED4.cathode, LED5.cathode, LED6.cathode, LED7.cathode, LED8.cathode, LED9.cathode, LED10.cathode, LED11.cathode, Composant1.GND, Composant1.D7
  N2: VCC1.+, Composant1.VIN
  N3: LED1.anode, R5.Pin_0
  N4: LED2.anode, R4.Pin_0
  N5: LED3.anode, R3.Pin_0
  N6: LED4.anode, R2.Pin_0, Composant1.A3
  N7: LED5.anode, R1.Pin_0
  N8: LED6.anode, R10.Pin_0
  N9: LED7.anode, R8.Pin_0
  N10: LED8.anode, R7.Pin_0
  N11: LED9.anode, R9.Pin_0
  N12: LED10.anode, R6.Pin_0
  N13: LED11.anode, R11.Pin_0
  N14: R1.Pin_1, Composant1.D2, Composant1.A2
  N15: R2.Pin_1, Composant1.D3, Composant1.D8
  N16: R3.Pin_1, Composant1.D4
  N17: R4.Pin_1, Composant1.D5
  N18: R6.Pin_1, Composant1.A1
  N19: R7.Pin_1, Composant1.D10
  N20: R9.Pin_1, Composant1.D11/MOSI
  N21: R11.Pin_1, Composant1.D12/MISO
  N22: Composant1.RESET, Composant1.D6

// code stored in the sketch: clockobin.ino
/*clockôbin by kerblock
   Date : 11/06/17
   Description : A clock for your mind. Display time in binary with leds.
*/

byte hour;
byte minute;
byte second;

boolean leds_test = false;

//D2->D6 = leds hours
//D7->D12 = leds minutes
void setup() {
  Serial.begin(9600);
  hour = 17;
  minute = 57;
  second = 30;

  for (byte i = 2; i <= 6; i++){
    pinMode(i, OUTPUT);
    if (leds_test){
    digitalWrite(i, HIGH);
    delay(500);
    digitalWrite(i, LOW);
    }
  }
  for (byte i = 7; i <= 12; i++){
    pinMode(i, OUTPUT);
    if (leds_test){
    digitalWrite(i, HIGH);
    delay(500);
    digitalWrite(i, LOW);
    }
  }
}

void loop() {
  updateTime();
  ledsRouter();
}

void updateTime(){
  delay(1000);
  second++;
  if (second > 59){
    second = 0;
    minute++;
  }
  if (minute > 59){
    minute = 0;
    hour++;
  }
  if (hour > 23){
    hour = 0;
  }
}

void ledsRouter(){
  String strH = String(hour, BIN);
  String strM = String(minute, BIN);

  //hour loop
  for (int i = 0; i < strH.length(); i++){
      if (strH.charAt(i) == '0'){
        digitalWrite(6-i, LOW);
      }
      else{
        digitalWrite(6-i, HIGH);
      }
    }

  //minute loop
  for (int i = 0; i < strM.length(); i++){
     if (strM.charAt(i) == '0'){
        digitalWrite(12-i, LOW);
      }
      else{
        digitalWrite(12-i, HIGH);
      }
  }
}
